# Fritzing sketch circult (saved by Fritzing 0.9.4)
breadboards: 1

parts:
  LED1 = LED - 3mm [color="Red (633nm)" package="3 mm [THT]"]
  R1 = Resistor [tolerance=±5% resistance=220 package="0402 [SMD]"]
  R2 = Resistor [tolerance=±5% resistance=220 package="0402 [SMD]"]
  LED2 = LED - 3mm [color="Red (633nm)" package="3 mm [THT]"]
  LED3 = LED - 3mm [color="Red (633nm)" package="3 mm [THT]"]
  R3 = Resistor [tolerance=±5% resistance=220 package="0402 [SMD]"]
  부품1 = Arduino Uno (Rev3) - ICSP

nets:
  N1: LED1.cathode, LED2.cathode, LED3.cathode, 부품1.GND
  N2: LED1.anode, R1.Pin_0
  N3: R1.Pin_1, 부품1.D3_PWM
  N4: R2.Pin_0, LED2.anode
  N5: R2.Pin_1, 부품1.D2
  N6: LED3.anode, R3.Pin_0
  N7: R3.Pin_1, 부품1.D4
