# Fritzing sketch circuit (saved by Fritzing 0.9.4)
breadboards: 1

parts:
  부품1 = Arduino Uno (Rev3)
  J1 = Basic Servo
  R1 = Resistor [tolerance=±5% resistance=220 package="0402 [SMD]"]
  LED1 = LED - 5mm [color="Red (633nm)" package="5 mm [THT]"]
  LED2 = LED - 5mm [color="Red (633nm)" package="5 mm [THT]"]
  R2 = Resistor [tolerance=±5% resistance=220 package="0402 [SMD]"]
  LED3 = RGB LED (com. cathode, rbg) [package="5 mm [THT]"]
  HC-SR04_Sensor_1 = HC-SR04 Ultrasonic Distance Sensor

nets:
  N1: 부품1.D8, J1.pulse
  N2: 부품1.D10_PWM/SS, HC-SR04_Sensor_1.ECHO
  N3: 부품1.D11_PWM/MOSI, HC-SR04_Sensor_1.TRIG
  N4: 부품1.D2, R1.Pin_1
  N5: 부품1.D3_PWM, R2.Pin_1
  N6: 부품1.D5_PWM, LED3.blue_anode
  N7: 부품1.D6_PWM, LED3.common_cathode
  N8: 부품1.D7, LED3.red_anode
  VCC: 부품1.5V, J1.vcc, HC-SR04_Sensor_1.VCC
  GND: 부품1.GND, J1.gnd, LED1.cathode, LED2.cathode, LED3.green_anode, HC-SR04_Sensor_1.GND
  N9: R1.Pin_0, LED1.anode
  N10: LED2.anode, R2.Pin_0
